# Fritzing sketch SensorLamp (saved by Fritzing 0.9.3b)
perfboards: 1

parts:
  C1 = Electrolytic Capacitor [capacitance=0.1mF package="100 mil [THT, electrolytic]"]
  LED1 = LED - 5mm [color="Red (633nm)" package="5 mm [THT]"]
  LED2 = LED - 5mm [color="Red (633nm)" package="5 mm [THT]"]
  LED3 = LED - 5mm [color="Red (633nm)" package="5 mm [THT]"]
  LED4 = LED - 5mm [color="Red (633nm)" package="5 mm [THT]"]
  R1 = Resistor [tolerance=±5% resistance=68k package=THT]
  R2 = Resistor [tolerance=±5% resistance=68k package=THT]
  R3 = Resistor [tolerance=±5% resistance=68 package=THT]
  R4 = Resistor [tolerance=±5% resistance=68 package=THT]
  R5 = Resistor [tolerance=±5% resistance=220 package=THT]
  Q1 = NPN-Transistor [package="TO92 [THT]"]
  J1 = Infrared Proximity Sensor
  Arduino_Nano_v3 = Arduino Nano (Rev3.0)

nets:
  GND: C1.-, Q1.E, J1.GND, Arduino_Nano_v3.GND
  VCC: C1.+, R1.Pin_0, R2.Pin_0, R3.Pin_0, R4.Pin_0, J1.Vcc, Arduino_Nano_v3.5V
  N1: LED1.cathode, LED2.cathode, LED3.cathode, LED4.cathode, Q1.C
  N2: LED1.anode, R1.Pin_1
  N3: LED2.anode, R2.Pin_1
  N4: LED3.anode, R3.Pin_1
  N5: LED4.anode, R4.Pin_1
  N6: R5.Pin_0, Arduino_Nano_v3.D12/MISO
  N7: R5.Pin_1, Q1.B
  N8: J1.Vout, Arduino_Nano_v3.A7
