# Fritzing sketch SensorLamp_v2 (saved by Fritzing 0.9.3b)
circuit board: 7.37914cm x 2.26478cm
perfboards: 1

parts:
  C1 = Electrolytic Capacitor [capacitance=0.1mF package="100 mil [THT, electrolytic]"]
  Q1 = NPN-Transistor [package="TO92 [THT]"]
  J1 = Infrared Proximity Sensor
  Arduino_Nano_v3 = Arduino Nano (Rev3.0)
  LED1 = Super Flux LED blue [color=White]
  LED2 = Super Flux LED blue [color=White]
  LED3 = Super Flux LED blue [color=White]
  LED4 = Super Flux LED blue [color=White]
  J2 = male pin header, 8 pins [form="♂ (male)"]
  R2 = Resistor [tolerance=±5% resistance=56 package=THT]
  R3 = Resistor [tolerance=±5% resistance=56 package=THT]
  R4 = Resistor [tolerance=±5% resistance=56 package=THT]
  R5 = Resistor [tolerance=±5% resistance=180 package=THT]
  R1 = Resistor [tolerance=±5% resistance=56 package=THT]
  J3 = male pin header, 2 pins [form="♂ (male)"]
  J4 = male pin header, 1 pin [form="♂ (male)"]

nets:
  GND: C1.-, Q1.E, J1.GND, Arduino_Nano_v3.GND, J3.pin2
  VCC: C1.+, J1.Vcc, Arduino_Nano_v3.5V, R2.Pin_0, R3.Pin_0, R4.Pin_0, R1.Pin_0, J3.pin1
  N1: Q1.B, R5.Pin_1
  N2: Q1.C, LED1.cathode, LED2.cathode, LED3.cathode, LED4.cathode, J2.pin2, J2.pin4, J2.pin6, J2.pin8
  N3: J1.Vout, Arduino_Nano_v3.A7, J4.pin1
  N4: Arduino_Nano_v3.D3, R5.Pin_0
  N5: LED1.anode, J2.pin1, R1.Pin_1
  N6: LED2.anode, J2.pin3, R2.Pin_1
  N7: LED3.anode, J2.pin5, R3.Pin_1
  N8: LED4.anode, J2.pin7, R4.Pin_1
